# Fritzing sketch PreventCataclysmSystems (saved by Fritzing 0.9.3b)
breadboards: 1

parts:
  DHT1 = DHT11 Humitidy and Temperature Sensor
  R1 = Resistor [tolerance=±5% resistance=2.2 package="0603 [SMD]"]
  IC1 = MCP3008 8-channel 10-bit ADC [part_number=MCP3008]
  Componente1 = Soil Moisture Sensor
  Componente3 = Triple Axis Accelerometer Breakout - ADXL345
  Raspberry_Pi1 = Raspberry Pi B+

nets:
  VCC: DHT1.VDD, R1.Pin_0, IC1.no_name_yet#15, IC1.no_name_yet#16, Componente1.VCC, Componente3.VCC, Componente3.SDA, Raspberry_Pi1.3v3, Raspberry_Pi1.GPIO2, Raspberry_Pi1.GPIO27, Raspberry_Pi1.GPIO22, Raspberry_Pi1.3V3
  GND: DHT1.DATA, DHT1.GND, R1.Pin_1, IC1.no_name_yet#9, IC1.no_name_yet#10, IC1.no_name_yet#14, Componente1.GND, Componente3.GND, Raspberry_Pi1.GPIO4, Raspberry_Pi1.GND, Raspberry_Pi1.GPIO17, Raspberry_Pi1.ID_SD, Raspberry_Pi1.GPIO5, Raspberry_Pi1.GPIO7, Raspberry_Pi1.GPIO8, Raspberry_Pi1.GPIO25
  N1: IC1.no_name_yet#6, Componente1.SIG
  N2: IC1.no_name_yet#11, Raspberry_Pi1.GPIO10
  N3: IC1.no_name_yet#12, Raspberry_Pi1.GPIO9
  N4: IC1.no_name_yet#13, Raspberry_Pi1.GPIO11
  N5: Componente3.SCL, Raspberry_Pi1.GPIO3

custom parts:
  DHT11 Humitidy and Temperature Sensor: DHT11 Humidity and Temperature Sensor
